// Digital circuit InstDecoder.dig as structural Verilog
module InstDecoder (
  input  [31:0] IW,
  output [1:0] ALUSrcB,
  output [2:0] ALUOp,
  output RFW,
  output WDsel,
  output PCsel,
  output ALUSrcA
);

  wire addi_1_eq, addr_1_eq, j_type_eq, jalr_1_eq, mul_1_eq;
  wire [2:0] INUM_num;

  ADDI addi_1 (.iw_opcode(IW[6:0]), .iw_funct3(IW[14:12]), .opcode(7'b0010011), .funct3(3'b000), .eq(addi_1_eq));
  ADDR addr_1 (
    .iw_opcode(IW[6:0]), .iw_funct3(IW[14:12]), .iw_funct7(IW[31:25]), .opcode(7'b0110011), .funct3(3'b000),
    .funct7({7{1'b0}}), .eq(addr_1_eq));
  Comparator #(.Bits(7)) j_type (.a(IW[6:0]), .b(7'b1101111), .eq(j_type_eq));  // open: gt, lt
  JALR jalr_1 (.iw_opcode(IW[6:0]), .iw_funct3(IW[14:12]), .opcode(7'b1100111), .funct3(3'b000), .eq(jalr_1_eq));
  MUL mul_1 (.iw_opcode(IW[6:0]), .iw_funct3(IW[14:12]), .opcode(7'b0110011), .funct3(3'b000), .eq(mul_1_eq));
  PriorityEncoder #(.Selector_Bits(3)) INUM (
    .in0(addi_1_eq), .in1(addr_1_eq), .in2(j_type_eq), .in3(jalr_1_eq), .in4(mul_1_eq), .in5(1'b0),
    .in6(1'b0), .in7(1'b0), .num(INUM_num));  // open: any
  ROM #(.AddrBits(3), .Bits(9)) rom_1 (.A(INUM_num), .sel(1'b1), .D({RFW, ALUOp, ALUSrcA, ALUSrcB, PCsel, WDsel}));

  // Other names for the same wires on the sheet: iw_opcode[6:0] = IW[6:0]; iw_f3[2:0] = IW[14:12];
  //   iw_f7[6:0] = IW[31:25]

  // Notes on the sheet:
  //   contents of rom_1 (hex, n*v repeats v):
  //   104,100,11b,107,140
endmodule
